# Fritzing sketch isp (saved by Fritzing 0.9.3b)
breadboards: 1

parts:
  Raspberry_Pi_1 = Raspberry Pi 3 [part_number=RPI-3-V1.2]
  J1 = female pin header, 2 pins [form="♀ (female)"]
  J2 = female pin header, 2 pins [form="♀ (female)"]
  J3 = female pin header, 2 pins [form="♀ (female)"]
  R2 = Resistor [tolerance=±5% resistance=1.5k package=THT]
  R1 = Resistor [tolerance=±5% resistance=2.7k package=THT]
  Q1 = Basic FET N-Channel [package="TO220 [THT]"]
  R3 = Resistor [tolerance=±5% resistance=10k package=THT]
  D1 = Rectifier Diode [part_number=1N4001 package="300 mil [THT]"]
  R4 = Resistor [tolerance=±5% resistance=10k package=THT]

nets (from the breadboard view):
  N1: Raspberry_Pi_1.3v3, Q1.drain, R3.Pin_1
  N2: Raspberry_Pi_1.GPIO3, Raspberry_Pi_1.GND, J1.pin1, R1.Pin_1
  N3: Raspberry_Pi_1.GIPO10, J2.pin1
  N4: Raspberry_Pi_1.GIPO9, R2.Pin_1, R1.Pin_0
  N5: Raspberry_Pi_1.GIPO11, J2.pin2
  N6: Raspberry_Pi_1.GIPO14, Q1.source, D1.cathode
  N7: J1.pin2, Q1.gate, R4.Pin_1
  N8: J3.pin1, R4.Pin_0
  N9: J3.pin2, R2.Pin_0
  N10: R3.Pin_0, D1.anode

notes:
  5 3 1
  6 4 2
